// Logisim project CPU.circ as structural Verilog
module main (
  input  [5:0] in_1,
  input  [15:0] in_2,
  input  Store
);

  wire Clear, Clock;
  wire [3:0] joystick_1_x, joystick_1_y;
  wire [4:0] adapter_1_selector, memoryconverter_1_out_7;
  wire [11:0] ROMAddress;
  wire [15:0] ROMData;
  wire [31:0] adapter_1_data_2, demultiplexer_1_out0, demultiplexer_1_out1, demultiplexer_1_out2,
       demultiplexer_1_out3, demultiplexer_1_out4, demultiplexer_1_out5, demultiplexer_1_out6,
       demultiplexer_1_out7, demultiplexer_1_out8, demultiplexer_1_out9, demultiplexer_1_out10,
       demultiplexer_1_out11, demultiplexer_1_out12, demultiplexer_1_out13, demultiplexer_1_out14,
       demultiplexer_1_out15, demultiplexer_1_out16, demultiplexer_1_out17, demultiplexer_1_out18,
       demultiplexer_1_out19, demultiplexer_1_out20, demultiplexer_1_out21, demultiplexer_1_out22,
       demultiplexer_1_out23, demultiplexer_1_out24, demultiplexer_1_out25, demultiplexer_1_out26,
       demultiplexer_1_out27, demultiplexer_1_out28, demultiplexer_1_out29, demultiplexer_1_out30,
       demultiplexer_1_out31, memoryconverter_1_out_6;

  ControllerAdapter controlleradapter_1 (.in_1(joystick_1_x), .in_2(joystick_1_y), .in_3(Store));  // open: out_4
  Joystick joystick_1 (.x(joystick_1_x), .y(joystick_1_y));
  Clock clock_1 (.out(Clock));
  Button button_1 (.out(Clear));
  ROM #(.addrWidth(12), .dataWidth(16)) rom_1 (.addr(ROMAddress), .data(ROMData));  // open: sel
  MemoryConverter memoryconverter_1 (
    .Data(in_2), .Address(in_1), .Store(Store), .Clock(Clock), .Clear(Clear),
    .out_6(memoryconverter_1_out_6), .out_7(memoryconverter_1_out_7));
  RAM #(.addrWidth(16), .dataWidth(16), .bus("separate")) ram_1 (
    .clk(Clock), .clr(Clear));  // open: addr, din, data, str, sel, ld
  DotMatrix #(.matrixcols(32), .matrixrows(32), .persist(64)) dotmatrix_1 (
    .col0(demultiplexer_1_out0), .col1(demultiplexer_1_out1), .col2(demultiplexer_1_out2),
    .col3(demultiplexer_1_out3), .col4(demultiplexer_1_out4), .col5(demultiplexer_1_out5),
    .col6(demultiplexer_1_out6), .col7(demultiplexer_1_out7), .col8(demultiplexer_1_out8),
    .col9(demultiplexer_1_out9), .col10(demultiplexer_1_out10), .col11(demultiplexer_1_out11),
    .col12(demultiplexer_1_out12), .col13(demultiplexer_1_out13), .col14(demultiplexer_1_out14),
    .col15(demultiplexer_1_out15), .col16(demultiplexer_1_out16), .col17(demultiplexer_1_out17),
    .col18(demultiplexer_1_out18), .col19(demultiplexer_1_out19), .col20(demultiplexer_1_out20),
    .col21(demultiplexer_1_out21), .col22(demultiplexer_1_out22), .col23(demultiplexer_1_out23),
    .col24(demultiplexer_1_out24), .col25(demultiplexer_1_out25), .col26(demultiplexer_1_out26),
    .col27(demultiplexer_1_out27), .col28(demultiplexer_1_out28), .col29(demultiplexer_1_out29),
    .col30(demultiplexer_1_out30), .col31(demultiplexer_1_out31));
  Adapter adapter_1 (
    .Addres(memoryconverter_1_out_7), .Data(memoryconverter_1_out_6), .Store(Store), .Clock(Clock),
    .Clear(Clear), .Data_2(adapter_1_data_2), .Selector(adapter_1_selector));
  Processador processador_1 (.Inst(ROMData), .Clock(Clock), .in_3(Clear), .NextLine(ROMAddress));
  Demultiplexer #(.select(5), .width(32)) demultiplexer_1 (
    .out0(demultiplexer_1_out0), .out1(demultiplexer_1_out1), .out2(demultiplexer_1_out2),
    .out3(demultiplexer_1_out3), .out4(demultiplexer_1_out4), .out5(demultiplexer_1_out5),
    .out6(demultiplexer_1_out6), .out7(demultiplexer_1_out7), .out8(demultiplexer_1_out8),
    .out9(demultiplexer_1_out9), .out10(demultiplexer_1_out10), .out11(demultiplexer_1_out11),
    .out12(demultiplexer_1_out12), .out13(demultiplexer_1_out13), .out14(demultiplexer_1_out14),
    .out15(demultiplexer_1_out15), .out16(demultiplexer_1_out16), .out17(demultiplexer_1_out17),
    .out18(demultiplexer_1_out18), .out19(demultiplexer_1_out19), .out20(demultiplexer_1_out20),
    .out21(demultiplexer_1_out21), .out22(demultiplexer_1_out22), .out23(demultiplexer_1_out23),
    .out24(demultiplexer_1_out24), .out25(demultiplexer_1_out25), .out26(demultiplexer_1_out26),
    .out27(demultiplexer_1_out27), .out28(demultiplexer_1_out28), .out29(demultiplexer_1_out29),
    .out30(demultiplexer_1_out30), .out31(demultiplexer_1_out31), .in(adapter_1_data_2),
    .sel(adapter_1_selector));  // open: en

  // Notes on the sheet:
  //   contents of rom_1 (hex, n*v repeats v):
  //   31ff 1b00 4001 9005 8001 8005
endmodule

module ULA (
  input  [15:0] A,
  input  [15:0] B,
  input  [3:0] Op,
  output [15:0] R,
  output out_5,
  output out_6
);

  wire [15:0] And, Complet, LeftShift, Not, Or, OutDec, OutDiv, OutInc, OutMul, OutSub, OutSum, RigthShift,
       Xor;

  Negator #(.width(16)) negator_1 (.in(A), .out(Complet));
  assign And = A & B;  // AND_Gate and_1, 16 bits wide
  assign Or = A | B;  // OR_Gate or_1, 16 bits wide
  assign Not = ~A;  // NOT_Gate not_1, 16 bits wide
  assign Xor = A ^ B;  // XOR_Gate xor_1, 16 bits wide
  Adder #(.width(16)) adder_1 (.a(A), .b(B), .out(OutSum));  // open: cin, cout
  Subtractor #(.width(16)) subtractor_1 (.a(A), .b(B), .out(OutSub));  // open: bin, bout
  Multiplier #(.width(16)) multiplier_1 (.a(A), .b(B), .out(OutMul));  // open: cin, cout
  Divider #(.width(16)) divider_1 (.a(A), .b(B), .out(OutDiv));  // open: upper, rem
  Shifter #(.width(16)) shifter_1 (.in(A), .\dist (B[3:0]), .out(LeftShift));
  Adder #(.width(16)) adder_2 (.a(A), .b(16'h1), .out(OutInc));  // open: cin, cout
  Subtractor #(.width(16)) subtractor_2 (.a(A), .b(16'h1), .out(OutDec));  // open: bin, bout
  Shifter #(.width(16), .shift("lr")) shifter_2 (.in(A), .\dist (B[3:0]), .out(RigthShift));
  Comparator #(.width(16)) comparator_1 (.a(A), .b(B), .gt(out_5), .eq(out_6));  // open: lt
  Multiplexer #(.select(4), .width(16)) multiplexer_1 (
    .in0(OutSum), .in1(OutSub), .in2(OutMul), .in3(OutDiv), .in4(LeftShift), .in5(RigthShift), .in6(Complet),
    .in7(And), .in8(Or), .in9(Not), .in10(Xor), .in11(OutInc), .in12(OutDec), .out(R), .sel(Op));  // open: in13, in14, in15, en
endmodule

module LatchSR (
  input  Set,
  input  Reset,
  output out_3
);

  wire and_1_out, and_2_out, not_2_out;

  and and_1 (and_1_out, Set, not_2_out);
  and and_2 (and_2_out, out_3, Reset);
  not not_1 (out_3, and_1_out);
  not not_2 (not_2_out, and_2_out);
endmodule

module LatchD (
  input  D,
  input  Enable,
  output out_3
);

  wire and_1_out, and_2_out, not_1_out, not_2_out, not_3_out;

  not not_1 (not_1_out, D);
  not not_2 (not_2_out, and_1_out);
  and and_1 (and_1_out, D, Enable);
  and and_2 (and_2_out, Enable, not_1_out);
  not not_3 (not_3_out, and_2_out);
  LatchSR latchsr_1 (.Set(not_2_out), .Reset(not_3_out), .out_3(out_3));
endmodule

module FlipFlop (
  input  D,
  input  Enable,
  input  Clock,
  output out_4
);

  wire and_1_out, latchd_1_out_3, not_1_out;

  and and_1 (and_1_out, Enable, Clock);
  not not_1 (not_1_out, Clock);
  LatchD latchd_1 (.D(D), .Enable(and_1_out), .out_3(latchd_1_out_3));
  LatchD latchd_2 (.D(latchd_1_out_3), .Enable(not_1_out), .out_3(out_4));
endmodule

module Reg (
  input  Clock,
  input  Enable,
  input  Reset,
  input  [3:0] AddresA,
  input  [3:0] AddresB,
  input  [15:0] Data,
  output [15:0] DataA,
  output [15:0] DataB
);

  wire en0, en1, en2, en3, en4, en5, en6, en7, en8, en9, en10, en11, en12, en13, en14, en15;
  wire [15:0] out0, out1, out2, out3, out4, out5, out6, out7, out8, out9, out10, out11, out12, out13, out14,
       out15;

  Demultiplexer #(.select(4)) demultiplexer_1 (
    .out0(en0), .out1(en1), .out2(en2), .out3(en3), .out4(en4), .out5(en5), .out6(en6), .out7(en7),
    .out8(en8), .out9(en9), .out10(en10), .out11(en11), .out12(en12), .out13(en13), .out14(en14),
    .out15(en15), .in(Enable), .sel(AddresA));  // open: en
  Register #(.width(16)) register_1 (.D(Data), .en(en0), .Q(out0), .clk(Clock), .clr(Reset));
  Register #(.width(16)) register_2 (.D(Data), .en(en1), .Q(out1), .clk(Clock), .clr(Reset));
  Register #(.width(16)) register_3 (.D(Data), .en(en3), .Q(out3), .clk(Clock), .clr(Reset));
  Register #(.width(16)) register_4 (.D(Data), .en(en4), .Q(out4), .clk(Clock), .clr(Reset));
  Register #(.width(16)) register_5 (.D(Data), .en(en5), .Q(out5), .clk(Clock), .clr(Reset));
  Register #(.width(16)) register_6 (.D(Data), .en(en6), .Q(out6), .clk(Clock), .clr(Reset));
  Register #(.width(16)) register_7 (.D(Data), .en(en7), .Q(out7), .clk(Clock), .clr(Reset));
  Register #(.width(16)) register_8 (.D(Data), .en(en8), .Q(out8), .clk(Clock), .clr(Reset));
  Multiplexer #(.select(4), .width(16)) multiplexer_1 (
    .in0(out0), .in1(out1), .in2(out2), .in3(out3), .in4(out4), .in5(out5), .in6(out6), .in7(out7),
    .in8(out8), .in9(out9), .in10(out10), .in11(out11), .in12(out12), .in13(out13), .in14(out14),
    .in15(out15), .out(DataA), .sel(AddresA));  // open: en
  Multiplexer #(.select(4), .width(16)) multiplexer_2 (
    .in0(out0), .in1(out1), .in2(out2), .in3(out3), .in4(out4), .in5(out5), .in6(out6), .in7(out7),
    .in8(out8), .in9(out9), .in10(out10), .in11(out11), .in12(out12), .in13(out13), .in14(out14),
    .in15(out15), .out(DataB), .sel(AddresB));  // open: en
  Register #(.width(16)) register_9 (.D(Data), .en(en9), .Q(out9), .clk(Clock), .clr(Reset));
  Register #(.width(16)) register_10 (.D(Data), .en(en10), .Q(out10), .clk(Clock), .clr(Reset));
  Register #(.width(16)) register_11 (.D(Data), .en(en11), .Q(out11), .clk(Clock), .clr(Reset));
  Register #(.width(16)) register_12 (.D(Data), .en(en12), .Q(out12), .clk(Clock), .clr(Reset));
  Register #(.width(16)) register_13 (.D(Data), .en(en15), .Q(out15), .clk(Clock), .clr(Reset));
  Register #(.width(16)) register_14 (.D(Data), .en(en2), .Q(out2), .clk(Clock), .clr(Reset));
  Register #(.width(16)) register_15 (.D(Data), .en(en13), .Q(out13), .clk(Clock), .clr(Reset));
  Register #(.width(16)) register_16 (.D(Data), .en(en14), .Q(out14), .clk(Clock), .clr(Reset));

  // Other names for the same wires on the sheet: addA[3:0] = AddresA; addB[3:0] = AddresB; clk = Clock; en = Enable;
  //   rst = Reset
endmodule

module Processador (
  input  [15:0] Inst,
  input  Clock,
  input  in_3,
  output [11:0] NextLine
);

  wire and_3_out, eq, gt, iscmp, iscmp0, iscmp1, isje, isjump, ismovconst, ismove, isop, not_1_out,
       not_2_out, not_3_out, not_4_out, not_5_out, not_6_out, not_7_out, not_8_out, not_9_out, not_10_out,
       not_11_out, not_12_out, not_13_out, not_14_out, not_15_out, not_16_out, or_1_out, or_2_out, regen,
       ula_1_out_5, ula_1_out_6;
  wire [3:0] a;
  wire [11:0] adder_1_out, next;
  wire [15:0] aout, bout, bulain, data, ulaout;

  Register #(.width(12)) PC (.D(next), .Q(NextLine), .clk(Clock), .clr(in_3));  // open: en
  not not_1 (not_1_out, Inst[13]);
  and and_1 (isop, Inst[12], not_1_out, not_2_out, not_3_out);
  not not_2 (not_2_out, Inst[14]);
  not not_3 (not_3_out, Inst[15]);
  not not_4 (not_4_out, Inst[12]);
  not not_5 (not_5_out, Inst[13]);
  and and_2 (isjump, not_4_out, not_5_out, not_6_out, Inst[15]);
  not not_6 (not_6_out, Inst[14]);
  and and_3 (and_3_out, isje, eq);
  and and_4 (ismove, Inst[12], Inst[13], not_7_out, Inst[15]);
  not not_7 (not_7_out, Inst[14]);
  not not_8 (not_8_out, Inst[12]);
  not not_9 (not_9_out, Inst[13]);
  not not_10 (not_10_out, Inst[15]);
  not not_11 (not_11_out, Inst[13]);
  and and_5 (iscmp1, Inst[12], not_11_out, Inst[14], not_12_out);
  not not_12 (not_12_out, Inst[15]);
  not not_13 (not_13_out, Inst[13]);
  and and_6 (isje, Inst[12], not_13_out, not_14_out, Inst[15]);
  not not_14 (not_14_out, Inst[14]);
  Adder #(.width(12)) adder_1 (.a(NextLine), .b(12'h1), .out(adder_1_out));  // open: cin, cout
  or or_1 (or_1_out, isjump, and_3_out);
  and and_7 (ismovconst, Inst[12], Inst[13], not_15_out, not_16_out);
  not not_15 (not_15_out, Inst[14]);
  not not_16 (not_16_out, Inst[15]);
  and and_8 (iscmp0, not_8_out, not_9_out, Inst[14], not_10_out);
  Multiplexer #(.width(12)) multiplexer_1 (
    .in0(adder_1_out), .in1(Inst[11:0]), .out(next), .sel(or_1_out));  // open: en
  Reg reg_1 (
    .Clock(Clock), .Enable(regen), .Reset(in_3), .AddresA(a), .AddresB(Inst[3:0]), .Data(data), .DataA(aout),
    .DataB(bout));
  // Probe on aout
  // Probe on bout
  // Probe on aout
  // Probe on bulain
  // Probe on data
  Multiplexer #(.width(16)) multiplexer_2 (
    .in0(ulaout), .in1({{8{1'b0}}, Inst[7:0]}), .out(data), .sel(ismovconst));  // open: en
  or or_2 (or_2_out, ismovconst, iscmp1);
  or or_3 (iscmp, iscmp0, iscmp1);
  // Probe on ulaout
  ULA ula_1 (.A(aout), .B(bulain), .R(ulaout), .Op(Inst[11:8]), .out_5(ula_1_out_5), .out_6(ula_1_out_6));
  or or_4 (regen, isop, ismovconst);
  Multiplexer #(.width(4)) multiplexer_3 (.in0(Inst[7:4]), .in1(Inst[11:8]), .out(a), .sel(or_2_out));  // open: en
  Multiplexer #(.width(16)) multiplexer_4 (
    .in0(bout), .in1({{8{1'b0}}, Inst[7:0]}), .out(bulain), .sel(iscmp1));  // open: en
  Register #(.width(1)) register_1 (.D(ula_1_out_5), .en(iscmp), .Q(gt), .clk(Clock), .clr(in_3));
  Register #(.width(1)) register_2 (.D(ula_1_out_6), .en(iscmp), .Q(eq), .clk(Clock), .clr(in_3));

  // Other names for the same wires on the sheet: aulain[15:0] = aout; clk = Clock; crr[11:0] = NextLine;
  //   s3[3:0] = Inst[15:12]; b[3:0] = Inst[3:0]; c[7:0] = Inst[7:0]; l[11:0] = Inst[11:0]; s0[3:0] = Inst[3:0];
  //   s1[3:0] = Inst[7:4]; p[3:0] = Inst[11:8]; s2[3:0] = Inst[11:8]; rst = in_3
endmodule

// rising
module Adapter (
  input  [4:0] Addres,
  input  [31:0] Data,
  input  Store,
  input  Clock,
  input  Clear,
  output [31:0] Data_2,
  output [4:0] Selector
);

  wire not_1_out, t_ff_1_q, t_ff_2_q, t_ff_3_q, t_ff_4_q;
  wire [4:0] multiplexer_1_out, t_ff_1_qn;
  wire [31:0] ram_1_data, ram_2_data;

  Multiplexer #(.width(5)) multiplexer_1 (
    .in0(Selector), .in1(Addres), .out(multiplexer_1_out), .sel(Store));  // open: en
  T_Flip_Flop t_ff_1 (.clk(Clock), .T(Clock), .Q(t_ff_1_q), .Qn(t_ff_1_qn[0]), .reset(Clear));  // open: preset, en
  RAM #(.addrWidth(5), .dataWidth(32), .bus("separate")) ram_1 (
    .addr(multiplexer_1_out), .din(Data), .data(ram_1_data), .str(Store), .clk(Clock), .clr(Clear));  // open: sel, ld
  T_Flip_Flop t_ff_2 (
    .clk(t_ff_1_q), .T(t_ff_1_q), .Q(t_ff_2_q), .Qn(t_ff_1_qn[1]), .reset(Clear));  // open: preset, en
  not not_1 (not_1_out, Store);
  T_Flip_Flop t_ff_3 (
    .clk(t_ff_2_q), .T(t_ff_2_q), .Q(t_ff_3_q), .Qn(t_ff_1_qn[2]), .reset(Clear));  // open: preset, en
  T_Flip_Flop t_ff_4 (
    .clk(t_ff_3_q), .T(t_ff_3_q), .Q(t_ff_4_q), .Qn(t_ff_1_qn[3]), .reset(Clear));  // open: preset, en
  T_Flip_Flop t_ff_5 (.clk(t_ff_4_q), .T(t_ff_4_q), .Qn(t_ff_1_qn[4]), .reset(Clear));  // open: Q, preset, en
  RAM #(.addrWidth(5), .dataWidth(32), .bus("separate")) ram_2 (
    .addr(Selector), .din(ram_1_data), .data(ram_2_data), .str(not_1_out), .clk(Clock), .clr(Clear));  // open: sel, ld
  Register #(.width(5)) register_1 (.D(t_ff_1_qn), .Q(Selector), .clk(Clock));  // open: en, clr
  Multiplexer #(.width(32)) multiplexer_2 (.in0(ram_2_data), .in1({32{1'b0}}), .out(Data_2), .sel(Clock));  // open: en

  // Other names for the same wires on the sheet: clr = Clear; str = Store
endmodule

module MemoryConverter (
  input  [15:0] Data,
  input  [5:0] Address,
  input  Store,
  input  Clock,
  input  Clear,
  output [31:0] out_6,
  output [4:0] out_7
);

  wire and_1_out, and_2_out, not_1_out;

  and and_1 (and_1_out, Address[0], Store);
  and and_2 (and_2_out, not_1_out, Store);
  RAM #(.addrWidth(5), .dataWidth(16), .bus("separate")) ram_1 (
    .addr(Address[5:1]), .din(Data), .data(out_6[15:0]), .str(and_1_out), .clk(Clock), .clr(Clear));  // open: sel, ld
  RAM #(.addrWidth(5), .dataWidth(16), .bus("separate")) ram_2 (
    .addr(Address[5:1]), .din(Data), .data(out_6[31:16]), .str(and_2_out), .clk(Clock), .clr(Clear));  // open: sel, ld
  not not_1 (not_1_out, Address[0]);

  assign out_7 = Address[5:1];

  // Other names for the same wires on the sheet: odd = Address[0]; str = Store
endmodule

module ControllerAdapter (
  input  [3:0] in_1,
  input  [3:0] in_2,
  input  in_3,
  output [15:0] out_4
);

  Register #(.width(16)) register_1 (.D({{8{1'b0}}, in_2, in_1}), .Q(out_4), .clk(in_3));  // open: en, clr
endmodule
